// Logisim project nand2tetris.circ as structural Verilog
module main (
  input  [15:0] in_1,
  input  in_2,
  input  in_3,
  input  in_4,
  input  in_5,
  input  [15:0] in_6,
  input  in_7,
  input  in_8,
  input  [15:0] in_9,
  input  in_10,
  input  in_11,
  input  in_12,
  output [15:0] out_13,
  output [15:0] out_14
);

  wire clock_1_out;

  ALU_16bit alu_16bit_1 (
    .InputX(in_1), .ZX(in_2), .NX(in_3), .F(in_4), .N0(in_5), .InputY(in_6), .ZY(in_7), .NY(in_8),
    .Output1(out_13));
  Clock clock_1 (.out(clock_1_out));
  PC_16bit pc_16bit_1 (
    .Input1(in_9), .Load(in_10), .Reset(in_11), .Increment(in_12), .Clock(clock_1_out), .out_6(out_14));
endmodule

module ALU_16bit (
  input  [15:0] InputX,
  input  ZX,
  input  NX,
  input  F,
  input  N0,
  input  [15:0] InputY,
  input  ZY,
  input  NY,
  output [15:0] Output1
);

  wire [15:0] adder_1_out, and_1_out, multiplexer_1_out, multiplexer_2_out, multiplexer_3_out,
       multiplexer_4_out, multiplexer_5_out, not_1_out, not_2_out, not_3_out;

  Multiplexer #(.width(16)) multiplexer_1 (.in0(InputX), .in1({16{1'b0}}), .out(multiplexer_1_out), .sel(ZX));
  Multiplexer #(.width(16)) multiplexer_2 (.in0(InputY), .in1({16{1'b0}}), .out(multiplexer_2_out), .sel(ZY));
  assign not_1_out = ~multiplexer_1_out;  // NOT_Gate not_1, 16 bits wide
  Multiplexer #(.width(16)) multiplexer_3 (.in0(multiplexer_2_out), .in1(not_2_out), .out(multiplexer_3_out), .sel(NY));
  assign not_2_out = ~multiplexer_2_out;  // NOT_Gate not_2, 16 bits wide
  Multiplexer #(.width(16)) multiplexer_4 (.in0(multiplexer_1_out), .in1(not_1_out), .out(multiplexer_4_out), .sel(NX));
  assign and_1_out = multiplexer_4_out & multiplexer_3_out;  // AND_Gate and_1, 16 bits wide
  Adder #(.width(16)) adder_1 (.a(multiplexer_4_out), .b(multiplexer_3_out), .out(adder_1_out));  // open: cin, cout
  Multiplexer #(.width(16)) multiplexer_5 (.in0(and_1_out), .in1(adder_1_out), .out(multiplexer_5_out), .sel(F));
  assign not_3_out = ~multiplexer_5_out;  // NOT_Gate not_3, 16 bits wide
  Multiplexer #(.width(16)) multiplexer_6 (.in0(multiplexer_5_out), .in1(not_3_out), .out(Output1), .sel(N0));
endmodule

module PC_16bit (
  input  [15:0] Input1,
  input  Load,
  input  Reset,
  input  Increment,
  input  Clock,
  output [15:0] out_6
);

  wire and_1_out, not_1_out, or_1_out;
  wire [15:0] adder_1_out, multiplexer_1_out, multiplexer_2_out, multiplexer_3_out;

  Multiplexer #(.width(16)) multiplexer_1 (.in0({16{1'b0}}), .in1(Input1), .out(multiplexer_1_out), .sel(Load));
  Adder #(.width(16)) adder_1 (.a(out_6), .b(16'h1), .out(adder_1_out));  // open: cin, cout
  Multiplexer #(.width(16)) multiplexer_2 (
    .in0(multiplexer_1_out), .in1(adder_1_out), .out(multiplexer_2_out), .sel(and_1_out));
  and and_1 (and_1_out, Increment, not_1_out);
  not not_1 (not_1_out, Load);
  Multiplexer #(.width(16)) multiplexer_3 (
    .in0(multiplexer_2_out), .in1({16{1'b0}}), .out(multiplexer_3_out), .sel(Reset));
  or or_1 (or_1_out, Load, Increment, Reset);
  Register #(.width(16)) register_1 (.D(multiplexer_3_out), .en(or_1_out), .clk(Clock), .Q(out_6));  // open: clr

  // Other names for the same wires on the sheet: Register_Output[15:0] = out_6
endmodule
